# Fritzing sketch MicroPython Rover wiring diagram (saved by Fritzing 0.9.2b)

parts:
  pyboard1 = Micro Python pyboard [part_number=PYBv10b]
  M2 = DC Motor
  Part4 = Bluetooth HC-05
  Part7 = BMP180 Breakout [part_number=SEN-11824]
  M3 = DC Motor
  PART2 = Motor Driver 1A Dual TB6612FNG [part_number=ROB_09457]
  Part9 = SparkFun 9 Degrees of Freedom Breakout - MPU-9150 [part_number=SEN-11486]
  U1 = LIPO-1000mAh [package=lipo-1000]
  Part10 = SRF04 Ultrasonic Rangefinder
  SERVO1 = Hitec HS-55 Servo [part_number=31055S]
  SERVO2 = Hitec HS-55 Servo [part_number=31055S]

nets:
  N1: pyboard1.P9A_GND, SERVO1.Ground
  N2: pyboard1.P9B_GND, SERVO2.Ground
  N3: pyboard1.P9C_GND, Part7.GND
  N4: pyboard1.P9D_GND, Part4.GND
  N5: pyboard1.P10A_VIN, SERVO1.Power
  N6: pyboard1.P10B_VIN, SERVO2.Power
  N7: pyboard1.X1, SERVO1.Signal
  N8: pyboard1.X2, SERVO2.Signal
  N9: pyboard1.X3, Part4.RXD
  N10: pyboard1.X4, Part4.TXD
  N11: pyboard1.X9, Part7.SCL
  N12: pyboard1.X10, Part7.SDA
  N13: pyboard1.X11, PART2.BIN1
  N14: pyboard1.X12, PART2.BIN2
  N15: pyboard1.X14_GND, Part10.GND
  N16: pyboard1.X15_3V3, Part7.3.3V, Part7.IO
  N17: pyboard1.X17_USR, PART2.STBY
  N18: pyboard1.X16_VIN, PART2.VCC
  N19: pyboard1.Y3, Part10.TRIG, Part10.MODE
  N20: pyboard1.Y4, Part10.ECHO
  N21: pyboard1.Y5, PART2.AIN2
  N22: pyboard1.Y6, PART2.AIN1
  N23: pyboard1.Y7, PART2.PWMA
  N24: pyboard1.Y8, PART2.PWMB
  N25: pyboard1.Y9, Part9.SCL
  N26: pyboard1.Y10, Part9.SDA
  N27: pyboard1.Y14_GND, Part9.GND
  VCC: pyboard1.Y15_3V3, Part4.VCC, Part9.VCC
  N28: pyboard1.Y16_VIN, Part10.VCC
  N29: M2.pin_1, PART2.A02
  N30: M2.pin_2, PART2.A01
  N31: M3.pin_1, PART2.B01
  N32: M3.pin_2, PART2.B02
  N33: PART2.VM, U1.+

custom parts:
  BMP180 Breakout: This is a breadboard friendly breakout board for the BMP180 high-precision, temp and pressure sensor.
  Motor Driver 1A Dual TB6612FNG: The TB6612FNG motor driver can control up to two DC motors at a constant current of 1.2A (3.2A peak). Two input signals (IN1 and IN2) can be used to control the motor in one of four function modes - CW, CCW, short-brake, and stop. The two motor outputs (A and B) can be separately controlled, the speed of each motor is controlled via a PWM input signal with a frequency up to 100kHz. The STBY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
  SparkFun 9 Degrees of Freedom Breakout - MPU-9150: The SparkFun 9DOF MPU-9150 is the world’s first 9-axis MotionTracking MEMS device designed for the low power, low cost, and high performance requirements of consumer electronics equipment including smartphones, tablets and wearable sensors. And guess what? You get to play with it. This breakout board makes it easy to prototype with the InvenSense MPU-9150 by breaking out all the pins you need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
  LIPO-1000mAh: 1000mAh Lipo-battery
  SRF04 Ultrasonic Rangefinder: http://www.robot-electronics.co.uk/htm/srf04tech.htm https://www.dfrobot.com/wiki/index.php?title=SRF05_Ultrasonic_sensor_(SKU:SEN0006)
  Hitec HS-55 Servo: HS-55 Economy Feather Servo Product Description The HS-55 set the standard for affordable performance, offering precision components that have been engineered to provide long lasting trouble free service! Featured in a hundred model aircraft reviews worldwide, the HS-55 is your best choice when it comes to controlling ”smaller” Electric’s and Park Flyers. Features Affordable Performance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
